// Logisim project LP-01.circ as structural Verilog: 4 circuits, main circuit main
module main (
  input  in_1,
  input  in_2,
  input  in_3,
  input  in_4,
  input  in_5,
  input  in_6,
  input  in_7,
  input  in_8,
  input  in_9
);

  _4bits_adder u_4bits_adder_1 (
    .in_2(in_1), .in_3(in_6), .in_4(in_2), .in_5(in_7), .in_6(in_4), .in_7(in_8), .in_8(in_5), .in_9(in_9),
    .Ci(in_3));  // open: S0, S1, S2, S3, Co
  _7_Segment_Display u_7_segment_display_1 ();  // open: g, f, a, b, e, d, c, dp
  _7_Segment_Display u_7_segment_display_2 ();  // open: g, f, a, b, e, d, c, dp
  _7_Segment_Display u_7_segment_display_3 ();  // open: g, f, a, b, e, d, c, dp
endmodule

module half_adder (
  input  A0,
  input  B0,
  output Soma,
  output Carry_out
);

  xor xor_1 (Soma, A0, B0);
  and and_1 (Carry_out, A0, B0);
endmodule

module full_adder (
  input  A0,
  input  B0,
  input  Ci0,
  output S0,
  output Co0
);

  wire _1_2_2_carry_out, _1_2_carry_out, _1_2_soma;

  half_adder _1_2 (.A0(A0), .B0(B0), .Soma(_1_2_soma), .Carry_out(_1_2_carry_out));
  half_adder _1_2_2 (.A0(_1_2_soma), .B0(Ci0), .Soma(S0), .Carry_out(_1_2_2_carry_out));
  or or_1 (Co0, _1_2_2_carry_out, _1_2_carry_out);
endmodule

module _4bits_adder (
  input  Ci,
  input  in_2,
  input  in_3,
  input  in_4,
  input  in_5,
  input  in_6,
  input  in_7,
  input  in_8,
  input  in_9,
  output S0,
  output S1,
  output S2,
  output S3,
  output Co
);

  wire full_adder_1_co0, full_adder_2_co0, full_adder_3_co0;

  full_adder full_adder_1 (.A0(in_2), .B0(in_3), .Ci0(Ci), .S0(S0), .Co0(full_adder_1_co0));
  full_adder full_adder_2 (.A0(in_4), .B0(in_5), .Ci0(full_adder_1_co0), .S0(S1), .Co0(full_adder_2_co0));
  full_adder full_adder_3 (.A0(in_6), .B0(in_7), .Ci0(full_adder_2_co0), .S0(S2), .Co0(full_adder_3_co0));
  full_adder full_adder_4 (.A0(in_8), .B0(in_9), .Ci0(full_adder_3_co0), .S0(S3), .Co0(Co));
endmodule
