// Logisim project LP_02.circ as structural Verilog: 1 circuit, main circuit main
module main (
  input  [3:0] in_1,
  input  [3:0] in_2,
  output [3:0] out_3,
  output [3:0] out_4
);

  wire [3:0] not_1_out, not_2_out, or_1_out;

  assign not_1_out = ~in_1;  // NOT_Gate not_1, 4 bits wide
  assign or_1_out = in_1 | in_2;  // OR_Gate or_1, 4 bits wide
  assign not_2_out = ~or_1_out;  // NOT_Gate not_2, 4 bits wide
  Multiplexer #(.select(4), .width(4), .enable("false")) multiplexer_1 (
    .in0(not_1_out), .in1(not_2_out), .out(out_3), .sel(out_4));  // open: in2, in3, in4, in5, in6, in7, in8, in9, in10, in11, in12, in13, in14, in15
endmodule
